// Logisim project project.circ as structural Verilog
module asset_memory (
  input  [3:0] addr,
  input  [3:0] column_num,
  output [11:0] column
);

  wire [2:0] multiplexer_1_out;
  wire [11:0] multiplexer_3_out, multiplexer_4_out, multiplexer_5_out, multiplexer_6_out, multiplexer_7_out,
       multiplexer_8_out, multiplexer_9_out, multiplexer_10_out;

  DotMatrix #(.matrixcols(12), .matrixrows(12)) dotmatrix_1 (
    .col0({12{1'b0}}), .col1({12{1'b0}}), .col2({12{1'b0}}), .col3({12{1'b0}}), .col4({12{1'b0}}),
    .col5({12{1'b0}}), .col6({12{1'b0}}), .col7({12{1'b0}}), .col8({12{1'b0}}), .col9({12{1'b0}}),
    .col10({12{1'b0}}), .col11({12{1'b0}}));
  DotMatrix #(.matrixcols(12), .matrixrows(12)) dotmatrix_2 (
    .col0({12{1'b0}}), .col1({12{1'b0}}), .col2({12{1'b0}}), .col3(12'h2), .col4(12'h30e), .col5(12'h7be),
    .col6(12'h7be), .col7(12'h30e), .col8(12'h2), .col9({12{1'b0}}), .col10({12{1'b0}}), .col11({12{1'b0}}));
  DotMatrix #(.matrixcols(12), .matrixrows(12)) dotmatrix_3 (
    .col0({12{1'b0}}), .col1({12{1'b0}}), .col2(12'hc0), .col3(12'h1c2), .col4(12'h86), .col5(12'h396),
    .col6(12'h7f6), .col7(12'h3f6), .col8(12'h1e2), .col9({12{1'b0}}), .col10({12{1'b0}}), .col11({12{1'b0}}));
  DotMatrix #(.matrixcols(12), .matrixrows(12)) dotmatrix_4 (
    .col0({12{1'b0}}), .col1({12{1'b0}}), .col2(12'h2), .col3(12'ha), .col4(12'h31a), .col5(12'h6fa),
    .col6(12'h5fa), .col7(12'h31a), .col8(12'ha), .col9(12'h2), .col10({12{1'b0}}), .col11({12{1'b0}}));
  Multiplexer #(.select(4), .width(3), .enable("false")) multiplexer_1 (
    .in0(3'b000), .in1(3'b000), .in2(3'b000), .in3(3'b000), .in4(3'b000), .in5(3'b000), .in6(3'b011),
    .in7(3'b000), .in8(3'b110), .in9(3'b000), .in10(3'b000), .in11(3'b101), .in12(3'b000), .in13(3'b100),
    .in14(3'b010), .in15(3'b001), .out(multiplexer_1_out), .sel(addr));
  Multiplexer #(.select(3), .width(12), .enable("false")) multiplexer_2 (
    .in0(multiplexer_3_out), .in1(multiplexer_4_out), .in2(multiplexer_5_out), .in3(multiplexer_6_out),
    .in4(multiplexer_10_out), .in5(multiplexer_9_out), .in6(multiplexer_8_out), .in7(multiplexer_7_out),
    .out(column), .sel(multiplexer_1_out));
  Multiplexer #(.select(4), .width(12), .enable("false")) multiplexer_3 (
    .in0({12{1'b0}}), .in1({12{1'b0}}), .in2({12{1'b0}}), .in3({12{1'b0}}), .in4({12{1'b0}}),
    .in5({12{1'b0}}), .in6({12{1'b0}}), .in7({12{1'b0}}), .in8({12{1'b0}}), .in9({12{1'b0}}),
    .in10({12{1'b0}}), .in11({12{1'b0}}), .out(multiplexer_3_out), .sel(column_num));  // open: in12, in13, in14, in15
  Multiplexer #(.select(4), .width(12), .enable("false")) multiplexer_4 (
    .in0({12{1'b0}}), .in1({12{1'b0}}), .in2({12{1'b0}}), .in3(12'h2), .in4(12'h30e), .in5(12'h7be),
    .in6(12'h7be), .in7(12'h30e), .in8(12'h2), .in9({12{1'b0}}), .in10({12{1'b0}}), .in11({12{1'b0}}),
    .out(multiplexer_4_out), .sel(column_num));  // open: in12, in13, in14, in15
  Multiplexer #(.select(4), .width(12), .enable("false")) multiplexer_5 (
    .in0({12{1'b0}}), .in1({12{1'b0}}), .in2(12'hc0), .in3(12'h1c2), .in4(12'h86), .in5(12'h396),
    .in6(12'h7f6), .in7(12'h3f6), .in8(12'h1e2), .in9({12{1'b0}}), .in10({12{1'b0}}), .in11({12{1'b0}}),
    .out(multiplexer_5_out), .sel(column_num));  // open: in12, in13, in14, in15
  Multiplexer #(.select(4), .width(12), .enable("false")) multiplexer_6 (
    .in0({12{1'b0}}), .in1({12{1'b0}}), .in2(12'h2), .in3(12'ha), .in4(12'h31a), .in5(12'h6fa),
    .in6(12'h5fa), .in7(12'h31a), .in8(12'ha), .in9(12'h2), .in10({12{1'b0}}), .in11({12{1'b0}}),
    .out(multiplexer_6_out), .sel(column_num));  // open: in12, in13, in14, in15
  Multiplexer #(.select(4), .width(12), .enable("false")) multiplexer_7 (
    .in0({12{1'b0}}), .in1({12{1'b0}}), .in2({12{1'b0}}), .in3(12'h180), .in4(12'h1b8), .in5(12'h70),
    .in6(12'h70), .in7(12'h1b8), .in8(12'h180), .in9({12{1'b0}}), .in10({12{1'b0}}), .in11({12{1'b0}}),
    .out(multiplexer_7_out), .sel(column_num));  // open: in12, in13, in14, in15
  Multiplexer #(.select(4), .width(12), .enable("false")) multiplexer_8 (
    .in0({12{1'b0}}), .in1({12{1'b0}}), .in2(12'he0), .in3(12'h72), .in4(12'hfa), .in5(12'h5fa),
    .in6(12'h5fa), .in7(12'hfa), .in8(12'h72), .in9(12'he0), .in10({12{1'b0}}), .in11({12{1'b0}}),
    .out(multiplexer_8_out), .sel(column_num));  // open: in12, in13, in14, in15
  Multiplexer #(.select(4), .width(12), .enable("false")) multiplexer_9 (
    .in0({12{1'b0}}), .in1(12'h1e0), .in2(12'h1b0), .in3(12'h15a), .in4(12'h9a), .in5(12'h7fa),
    .in6(12'h7fa), .in7(12'h9a), .in8(12'h15a), .in9(12'h1b0), .in10(12'h1e0), .in11({12{1'b0}}),
    .out(multiplexer_9_out), .sel(column_num));  // open: in12, in13, in14, in15
  Multiplexer #(.select(4), .width(12), .enable("false")) multiplexer_10 (
    .in0({12{1'b0}}), .in1({12{1'b0}}), .in2(12'h2), .in3(12'h60a), .in4(12'h2fa), .in5(12'h6fa),
    .in6(12'h6fa), .in7(12'h2fa), .in8(12'h60a), .in9(12'h2), .in10({12{1'b0}}), .in11({12{1'b0}}),
    .out(multiplexer_10_out), .sel(column_num));  // open: in12, in13, in14, in15
  DotMatrix #(.matrixcols(12), .matrixrows(12)) dotmatrix_5 (
    .col0({12{1'b0}}), .col1({12{1'b0}}), .col2({12{1'b0}}), .col3(12'h180), .col4(12'h1b8), .col5(12'h70),
    .col6(12'h70), .col7(12'h1b8), .col8(12'h180), .col9({12{1'b0}}), .col10({12{1'b0}}), .col11({12{1'b0}}));
  DotMatrix #(.matrixcols(12), .matrixrows(12)) dotmatrix_6 (
    .col0({12{1'b0}}), .col1({12{1'b0}}), .col2(12'he0), .col3(12'h72), .col4(12'hfa), .col5(12'h5fa),
    .col6(12'h5fa), .col7(12'hfa), .col8(12'h72), .col9(12'he0), .col10({12{1'b0}}), .col11({12{1'b0}}));
  DotMatrix #(.matrixcols(12), .matrixrows(12)) dotmatrix_7 (
    .col0({12{1'b0}}), .col1(12'h1e0), .col2(12'h1b0), .col3(12'h15a), .col4(12'h9a), .col5(12'h7fa),
    .col6(12'h7fa), .col7(12'h9a), .col8(12'h15a), .col9(12'h1b0), .col10(12'h1e0), .col11({12{1'b0}}));
  DotMatrix #(.matrixcols(12), .matrixrows(12)) dotmatrix_8 (
    .col0({12{1'b0}}), .col1({12{1'b0}}), .col2(12'h2), .col3(12'h60a), .col4(12'h2fa), .col5(12'h6fa),
    .col6(12'h6fa), .col7(12'h2fa), .col8(12'h60a), .col9(12'h2), .col10({12{1'b0}}), .col11({12{1'b0}}));
endmodule

module system_board (
  input  [15:0] stepIN,
  input  IOsignal,
  input  hold,
  input  clk,
  output [2:0] status,
  output castling,
  output color,
  output ready,
  output step_inspected,
  output [21:0] stepOUT
);

  wire and_1_out, comparator_1_eq, IOsel, IRQ, mem, not_1_out, not_2_out, read, sel, word;
  wire [1:0] status_t;
  wire [14:0] fp;
  wire [15:0] addr, cdm_16_1_p20, cdm_16_1_p21, data_bus, IN_q, pc, ps, r0, r1, r2, r3, r4, sp;
  wire [15:11] r5, r6;

  // Probe on {step_inspected, fp[14:5], color, castling, fp[2:0]}
  // Probe on {r6, stepOUT[21:11]}
  // Probe on {r5, stepOUT[10:0]}
  // Probe on r4
  // Probe on r3
  // Probe on r2
  // Probe on r1
  // Probe on r0
  // CdM_16 cdm_16_1: pin names not known; wires that end beside it: IRQ, hold, r0, r1, clk, r2, r3, r4, status_t, {r5, stepOUT[10:0]}, {r6, stepOUT[21:11]}, {step_inspected, fp[14:5], color, castling, fp[2:0]}, pc, sp, ps, mem, read, word, addr, cdm_16_1_p20, cdm_16_1_p21
  // Probe on status_t
  // Probe on pc
  // Probe on sp
  // Probe on ps
  not not_1 (not_1_out, read);
  assign data_bus = not_1_out ? cdm_16_1_p20 : 16'bz;  // Controlled_Buffer controlled_buffer_1
  assign cdm_16_1_p21 = read ? data_bus : 16'bz;  // Controlled_Buffer controlled_buffer_2
  // Probe on {r6, stepOUT[21:11]}
  // Probe on r4
  // Probe on r2
  // Probe on r0
  // RAM ram_1: pin names not known; wires that end beside it: addr, word, sel, clk, read, data_bus
  // Probe on {step_inspected, fp[14:5], color, castling, fp[2:0]}
  // Probe on {r5, stepOUT[10:0]}
  // Probe on r3
  // Probe on r1
  and and_1 (and_1_out, status_t[0], ~status_t[1]);  // AND_Gate
  Comparator #(.width(16)) comparator_1 (.a(16'h1234), .b(addr), .eq(comparator_1_eq));  // open: gt, lt
  and and_2 (IOsel, comparator_1_eq, mem);
  Register #(.width(16)) IN (.D(stepIN), .en(ready), .Q(IN_q), .clk(IOsignal));  // open: clr
  D_Flip_Flop #(.trigger("falling")) d_ff_1 (
    .clk(IOsignal), .D(and_1_out), .Q(IRQ), .reset(not_2_out));  // open: Qn, preset, en
  not not_2 (not_2_out, and_1_out);
  and and_3 (sel, ~IOsel, mem);  // AND_Gate
  assign data_bus = IOsel ? IN_q : 16'bz;  // Controlled_Buffer controlled_buffer_3
  and and_4 (ready, status_t[0], ~status_t[1], fp[14]);  // AND_Gate
  assign status = ready ? fp[2:0] : 3'bz;  // Controlled_Buffer controlled_buffer_4

  // Other names for the same wires on the sheet: fp (some bits) = {step_inspected, color, castling};
  //   r5[10:0] = stepOUT[10:0]; r6[10:0] = stepOUT[21:11]

  // Notes on the sheet:
  //   IOaddr
  //   Interrupt down
  //   if status = 1 & r7_14 = 1
endmodule

module newMain (
);

  wire a1, a2, a3, a4, a5, a6, a7, a8, b1, b2, b3, b4, b5, b6, b7, b8, button_3_out, button_4_out,
       button_5_out, button_34_out, button_signal, c1, c2, c3, c4, c5, c6, c7, c8, castling, clk, color,
       colour, counter_1_carry, current_cell, d1, d2, d3, d4, d5, d6, d7, d8, d_ff_1_q, e1, e2, e3, e4, e5,
       e6, e7, e8, enable, \end , enter, f1, f2, f3, f4, f5, f6, f7, f8, figure_signal, g1, g2, g3, g4, g5,
       g6, g7, g8, h1, h2, h3, h4, h5, h6, h7, h8, inspect, keyboard_1_avail, or_1_out, or_2_out, or_3_out,
       ready, reset;
  wire [1:0] button_1_out, button_31_out;
  wire [1:1] counter_2_q;
  wire [2:0] digit, letter, status;
  wire [3:0] bit_extender_1_out, button_figure, curr_coulumn, figure;
  wire [6:0] keyboard_1_data, lastmove_1__1, lastmove_1__2, lastmove_1__3, lastmove_1__4, lastmove_1__5,
       lastmove_1__6, lastmove_1_out_3, lastmove_1_out_4, lastmove_1_out_5, lastmove_1_out_6,
       lastmove_1_out_8, lastmove_1_out_9, lastmove_1_out_10, lastmove_1_out_11, lastmove_1_out_13,
       lastmove_1_out_14, lastmove_1_out_15, lastmove_1_out_16, lastmove_1_out_18, lastmove_1_out_19,
       lastmove_1_out_20, lastmove_1_out_21, lastmove_1_out_23, lastmove_1_out_24, lastmove_1_out_25,
       lastmove_1_out_26, lastmove_1_out_28, lastmove_1_out_29, lastmove_1_out_30, lastmove_1_out_31;
  wire [7:4] button_32_out;
  wire [10:5] multiplexer_2_out;
  wire [11:0] _12_bit;
  wire [15:0] button_ident_1_step_info, identmove_1_out_4, \input ;
  wire [21:0] system_board_1_stepout;

  test test_1 ();
  DotMatrix #(.matrixcols(6)) dotmatrix_1 (
    .col0(lastmove_1__1), .col1(lastmove_1__2), .col2(lastmove_1__3), .col3(lastmove_1__4),
    .col4(lastmove_1__5), .col5(lastmove_1__6));
  LastMove lastmove_1 (
    .in_1(\input ), ._1(lastmove_1__1), .out_3(lastmove_1_out_3), .out_4(lastmove_1_out_4),
    .out_5(lastmove_1_out_5), .out_6(lastmove_1_out_6), ._2(lastmove_1__2), .out_8(lastmove_1_out_8),
    .out_9(lastmove_1_out_9), .out_10(lastmove_1_out_10), .out_11(lastmove_1_out_11), ._3(lastmove_1__3),
    .out_13(lastmove_1_out_13), .out_14(lastmove_1_out_14), .out_15(lastmove_1_out_15),
    .out_16(lastmove_1_out_16), ._4(lastmove_1__4), .out_18(lastmove_1_out_18), .out_19(lastmove_1_out_19),
    .out_20(lastmove_1_out_20), .out_21(lastmove_1_out_21), ._5(lastmove_1__5), .out_23(lastmove_1_out_23),
    .out_24(lastmove_1_out_24), .out_25(lastmove_1_out_25), .out_26(lastmove_1_out_26), ._6(lastmove_1__6),
    .out_28(lastmove_1_out_28), .out_29(lastmove_1_out_29), .out_30(lastmove_1_out_30),
    .out_31(lastmove_1_out_31));
  // Probe on \input 
  Keyboard keyboard_1 (.clk(clk), .clr(or_1_out), .avail(keyboard_1_avail), .data(keyboard_1_data));  // open: re
  Clock clock_1 (.out(clk));
  Hex_Digit_Display hex_digit_display_1 (.value(bit_extender_1_out));  // open: dp
  assign bit_extender_1_out = {{1{1'b0}}, status};  // Bit_Extender bit_extender_1
  DotMatrix #(.matrixcols(6)) dotmatrix_2 (
    .col0(lastmove_1_out_4), .col1(lastmove_1_out_9), .col2(lastmove_1_out_14), .col3(lastmove_1_out_19),
    .col4(lastmove_1_out_24), .col5(lastmove_1_out_29));
  or or_1 (or_1_out, reset, enter);
  // Probe on letter
  // Probe on digit
  or or_2 (or_2_out, button_signal, figure_signal);
  Button u_reset (.out(reset));
  Button u_enter (.out(enter));
  DotMatrix #(.matrixcols(6)) dotmatrix_3 (
    .col0(lastmove_1_out_3), .col1(lastmove_1_out_8), .col2(lastmove_1_out_13), .col3(lastmove_1_out_18),
    .col4(lastmove_1_out_23), .col5(lastmove_1_out_28));
  IdentMove identmove_1 (
    .symbol(keyboard_1_data), .out_4(identmove_1_out_4), .symbol_update(keyboard_1_avail), .reset(or_1_out));
  D_Flip_Flop d_ff_1 (.Q(d_ff_1_q), .preset(or_2_out), .reset(keyboard_1_avail));  // open: clk, D, Qn, en
  or or_3 (or_3_out, \end , enter);
  system_board system_board_1 (
    .stepIN(\input ), .IOsignal(or_3_out), .clk(clk), .castling(castling), .step_inspected(inspect),
    .stepOUT(system_board_1_stepout), .status(status), .color(color), .ready(ready));  // open: hold
  Button button_1 (.out(button_1_out[0]));
  Button button_2 (.out(button_1_out[1]));
  Button button_3 (.out(button_3_out));
  Button button_4 (.out(button_4_out));
  Button button_5 (.out(button_5_out));
  Button button_6 (.out(a8));
  Button button_7 (.out(c8));
  Button button_8 (.out(b8));
  Button button_9 (.out(b7));
  Button button_10 (.out(a7));
  Button button_11 (.out(c7));
  Button button_12 (.out(a6));
  Button button_13 (.out(c6));
  Button button_14 (.out(b6));
  Button button_15 (.out(c5));
  Button button_16 (.out(b5));
  Button button_17 (.out(a5));
  Button button_18 (.out(b4));
  Button button_19 (.out(c4));
  Button button_20 (.out(a4));
  Button button_21 (.out(b3));
  Button button_22 (.out(c3));
  Button button_23 (.out(a3));
  Button button_24 (.out(c2));
  Button button_25 (.out(a2));
  Button button_26 (.out(b2));
  Button button_27 (.out(b1));
  Button button_28 (.out(a1));
  Button button_29 (.out(c1));
  DotMatrix #(.matrixcols(6)) dotmatrix_4 (
    .col0(lastmove_1_out_5), .col1(lastmove_1_out_10), .col2(lastmove_1_out_15), .col3(lastmove_1_out_20),
    .col4(lastmove_1_out_25), .col5(lastmove_1_out_30));
  button_ident button_ident_1 (
    .figure(button_figure), .button({digit, letter}), .update(button_signal), .figure_update(figure_signal),
    .reset(or_1_out), .step_info(button_ident_1_step_info));
  Button button_30 (.out(button_32_out[5]));
  Button button_31 (.out(button_31_out[0]));
  Button button_32 (.out(button_32_out[4]));
  Button button_33 (.out(button_31_out[1]));
  figure_pad figure_pad_1 (
    .Knight(button_5_out), .Bishop(button_4_out), .Rock(button_3_out), .Queen(button_34_out),
    .figure(button_figure), .figure_signal(figure_signal));
  Button button_34 (.out(button_34_out));
  Button button_35 (.out(g8));
  Button button_36 (.out(d8));
  Button button_37 (.out(e8));
  Button button_38 (.out(f8));
  Button button_39 (.out(g7));
  Button button_40 (.out(e7));
  Button button_41 (.out(d7));
  Button button_42 (.out(f7));
  Button button_43 (.out(e6));
  Button button_44 (.out(d6));
  Button button_45 (.out(f6));
  Button button_46 (.out(g6));
  Button button_47 (.out(f5));
  Button button_48 (.out(e5));
  Button button_49 (.out(d5));
  Button button_50 (.out(g5));
  Button button_51 (.out(d4));
  Button button_52 (.out(e4));
  Button button_53 (.out(f4));
  Button button_54 (.out(g4));
  Button button_55 (.out(g3));
  Button button_56 (.out(e3));
  Button button_57 (.out(d3));
  Button button_58 (.out(f3));
  Button button_59 (.out(f2));
  Button button_60 (.out(d2));
  Button button_61 (.out(g2));
  Button button_62 (.out(e2));
  Button button_63 (.out(f1));
  Button button_64 (.out(d1));
  Button button_65 (.out(g1));
  Button button_66 (.out(e1));
  DotMatrix #(.matrixcols(6)) dotmatrix_5 (
    .col0(lastmove_1_out_6), .col1(lastmove_1_out_11), .col2(lastmove_1_out_16), .col3(lastmove_1_out_21),
    .col4(lastmove_1_out_26), .col5(lastmove_1_out_31));
  Multiplexer #(.width(16), .enable("false")) multiplexer_1 (
    .in0(identmove_1_out_4), .in1(button_ident_1_step_info), .out(\input ), .sel(d_ff_1_q));
  Button button_67 (.out(button_32_out[7]));
  Button button_68 (.out(button_32_out[6]));
  DotMatrix #(.matrixcols(16), .matrixrows(15)) dotmatrix_6 ();  // open: col0, col1, col2, col3, col4, col5, col6, col7, col8, col9, col10, col11, col12, col13, col14, col15
  DotMatrix #(.matrixcols(16), .matrixrows(16)) dotmatrix_7 ();  // open: col0, col1, col2, col3, col4, col5, col6, col7, col8, col9, col10, col11, col12, col13, col14, col15
  // _2_matrix_field 2_matrix_field_1: pin names not known
  DotMatrix #(.matrixcols(16), .matrixrows(15)) dotmatrix_8 ();  // open: col0, col1, col2, col3, col4, col5, col6, col7, col8, col9, col10, col11, col12, col13, col14, col15
  DotMatrix #(.matrixcols(16), .matrixrows(16)) dotmatrix_9 ();  // open: col0, col1, col2, col3, col4, col5, col6, col7, col8, col9, col10, col11, col12, col13, col14, col15
  DotMatrix #(.matrixcols(16), .matrixrows(15)) dotmatrix_10 ();  // open: col0, col1, col2, col3, col4, col5, col6, col7, col8, col9, col10, col11, col12, col13, col14, col15
  DotMatrix #(.matrixcols(16), .matrixrows(16)) dotmatrix_11 ();  // open: col0, col1, col2, col3, col4, col5, col6, col7, col8, col9, col10, col11, col12, col13, col14, col15
  DotMatrix #(.matrixcols(16), .matrixrows(15)) dotmatrix_12 ();  // open: col0, col1, col2, col3, col4, col5, col6, col7, col8, col9, col10, col11, col12, col13, col14, col15
  DotMatrix #(.matrixcols(16), .matrixrows(16)) dotmatrix_13 ();  // open: col0, col1, col2, col3, col4, col5, col6, col7, col8, col9, col10, col11, col12, col13, col14, col15
  DotMatrix #(.matrixcols(16), .matrixrows(15)) dotmatrix_14 ();  // open: col0, col1, col2, col3, col4, col5, col6, col7, col8, col9, col10, col11, col12, col13, col14, col15
  DotMatrix #(.matrixcols(16), .matrixrows(16)) dotmatrix_15 ();  // open: col0, col1, col2, col3, col4, col5, col6, col7, col8, col9, col10, col11, col12, col13, col14, col15
  Button button_69 (.out(h8));
  Button button_70 (.out(h7));
  DotMatrix #(.matrixcols(16), .matrixrows(15)) dotmatrix_16 ();  // open: col0, col1, col2, col3, col4, col5, col6, col7, col8, col9, col10, col11, col12, col13, col14, col15
  DotMatrix #(.matrixcols(16), .matrixrows(16)) dotmatrix_17 ();  // open: col0, col1, col2, col3, col4, col5, col6, col7, col8, col9, col10, col11, col12, col13, col14, col15
  Button button_71 (.out(h6));
  Button button_72 (.out(h5));
  Button button_73 (.out(h4));
  Button button_74 (.out(h3));
  Button button_75 (.out(h2));
  Button button_76 (.out(h1));
  DotMatrix #(.matrixcols(16), .matrixrows(15)) dotmatrix_18 ();  // open: col0, col1, col2, col3, col4, col5, col6, col7, col8, col9, col10, col11, col12, col13, col14, col15
  DotMatrix #(.matrixcols(16), .matrixrows(16)) dotmatrix_19 ();  // open: col0, col1, col2, col3, col4, col5, col6, col7, col8, col9, col10, col11, col12, col13, col14, col15
  DotMatrix #(.matrixcols(16), .matrixrows(15)) dotmatrix_20 ();  // open: col0, col1, col2, col3, col4, col5, col6, col7, col8, col9, col10, col11, col12, col13, col14, col15
  DotMatrix #(.matrixcols(16), .matrixrows(16)) dotmatrix_21 ();  // open: col0, col1, col2, col3, col4, col5, col6, col7, col8, col9, col10, col11, col12, col13, col14, col15
  // Probe on status
  Multiplexer #(.width(11), .disabled(0)) multiplexer_2 (
    .in0(system_board_1_stepout[10:0]), .in1(system_board_1_stepout[21:11]),
    .out({multiplexer_2_out, colour, figure}), .sel(current_cell), .en(enable));
  button_pad button_pad_1 (
    .in_1(a8), .in_2(b8), .in_3(c8), .in_4(d8), .in_5(e8), .in_6(f8), .in_7(g8), .in_8(h8), .in_9(a7),
    .in_10(b7), .in_11(c7), .in_12(d7), .in_13(e7), .in_14(f7), .in_15(g7), .in_16(h7), .in_17(a6),
    .in_18(b6), .in_19(c6), .in_20(d6), .in_21(e6), .in_22(f6), .in_23(g6), .in_24(h6), .in_25(a5),
    .in_26(b5), .in_27(c5), .in_28(d5), .in_29(e5), .in_30(f5), .in_31(g5), .in_32(h5), .in_33(a4),
    .in_34(b4), .in_35(c4), .in_36(d4), .in_37(e4), .in_38(f4), .in_39(g4), .in_40(h4), .in_41(a3),
    .in_42(b3), .in_43(c3), .in_44(d3), .in_45(e3), .in_46(f3), .in_47(g3), .in_48(h3), .in_49(a2),
    .in_50(b2), .in_51(c2), .in_52(d2), .in_53(e2), .in_54(f2), .in_55(g2), .in_56(h2), .in_57(a1),
    .in_58(b1), .in_59(c1), .in_60(d1), .in_61(e1), .in_62(f1), .in_63(g1), .in_64(h1), .X(letter),
    .Y(digit), .pressed(button_signal));
  asset_memory asset_memory_1 (.column(_12_bit), .addr(figure), .column_num(curr_coulumn));
  DotMatrix #(.matrixcols(16), .matrixrows(15)) dotmatrix_22 ();  // open: col0, col1, col2, col3, col4, col5, col6, col7, col8, col9, col10, col11, col12, col13, col14, col15
  DotMatrix #(.matrixcols(16), .matrixrows(16)) dotmatrix_23 ();  // open: col0, col1, col2, col3, col4, col5, col6, col7, col8, col9, col10, col11, col12, col13, col14, col15
  DotMatrix #(.matrixcols(16), .matrixrows(15)) dotmatrix_24 ();  // open: col0, col1, col2, col3, col4, col5, col6, col7, col8, col9, col10, col11, col12, col13, col14, col15
  DotMatrix #(.matrixcols(16), .matrixrows(16)) dotmatrix_25 ();  // open: col0, col1, col2, col3, col4, col5, col6, col7, col8, col9, col10, col11, col12, col13, col14, col15
  DotMatrix #(.matrixcols(16), .matrixrows(15)) dotmatrix_26 ();  // open: col0, col1, col2, col3, col4, col5, col6, col7, col8, col9, col10, col11, col12, col13, col14, col15
  DotMatrix #(.matrixcols(16), .matrixrows(16)) dotmatrix_27 ();  // open: col0, col1, col2, col3, col4, col5, col6, col7, col8, col9, col10, col11, col12, col13, col14, col15
  DotMatrix #(.matrixcols(16), .matrixrows(15)) dotmatrix_28 ();  // open: col0, col1, col2, col3, col4, col5, col6, col7, col8, col9, col10, col11, col12, col13, col14, col15
  DotMatrix #(.matrixcols(16), .matrixrows(16)) dotmatrix_29 ();  // open: col0, col1, col2, col3, col4, col5, col6, col7, col8, col9, col10, col11, col12, col13, col14, col15
  DotMatrix #(.matrixcols(16), .matrixrows(15)) dotmatrix_30 ();  // open: col0, col1, col2, col3, col4, col5, col6, col7, col8, col9, col10, col11, col12, col13, col14, col15
  DotMatrix #(.matrixcols(16), .matrixrows(16)) dotmatrix_31 ();  // open: col0, col1, col2, col3, col4, col5, col6, col7, col8, col9, col10, col11, col12, col13, col14, col15
  DotMatrix #(.matrixcols(16), .matrixrows(15)) dotmatrix_32 ();  // open: col0, col1, col2, col3, col4, col5, col6, col7, col8, col9, col10, col11, col12, col13, col14, col15
  DotMatrix #(.matrixcols(16), .matrixrows(16)) dotmatrix_33 ();  // open: col0, col1, col2, col3, col4, col5, col6, col7, col8, col9, col10, col11, col12, col13, col14, col15
  DotMatrix #(.matrixcols(16), .matrixrows(15)) dotmatrix_34 ();  // open: col0, col1, col2, col3, col4, col5, col6, col7, col8, col9, col10, col11, col12, col13, col14, col15
  DotMatrix #(.matrixcols(16), .matrixrows(16)) dotmatrix_35 ();  // open: col0, col1, col2, col3, col4, col5, col6, col7, col8, col9, col10, col11, col12, col13, col14, col15
  DotMatrix #(.matrixcols(16), .matrixrows(15)) dotmatrix_36 ();  // open: col0, col1, col2, col3, col4, col5, col6, col7, col8, col9, col10, col11, col12, col13, col14, col15
  DotMatrix #(.matrixcols(16), .matrixrows(16)) dotmatrix_37 ();  // open: col0, col1, col2, col3, col4, col5, col6, col7, col8, col9, col10, col11, col12, col13, col14, col15
  // Probe on multiplexer_2_out
  // Probe on letter
  // Probe on curr_coulumn
  // Probe on digit
  DotMatrix #(.matrixcols(16), .matrixrows(15)) dotmatrix_38 ();  // open: col0, col1, col2, col3, col4, col5, col6, col7, col8, col9, col10, col11, col12, col13, col14, col15
  DotMatrix #(.matrixcols(16), .matrixrows(16)) dotmatrix_39 ();  // open: col0, col1, col2, col3, col4, col5, col6, col7, col8, col9, col10, col11, col12, col13, col14, col15
  DotMatrix #(.matrixcols(16), .matrixrows(15)) dotmatrix_40 ();  // open: col0, col1, col2, col3, col4, col5, col6, col7, col8, col9, col10, col11, col12, col13, col14, col15
  DotMatrix #(.matrixcols(16), .matrixrows(16)) dotmatrix_41 ();  // open: col0, col1, col2, col3, col4, col5, col6, col7, col8, col9, col10, col11, col12, col13, col14, col15
  DotMatrix #(.matrixcols(16), .matrixrows(15)) dotmatrix_42 ();  // open: col0, col1, col2, col3, col4, col5, col6, col7, col8, col9, col10, col11, col12, col13, col14, col15
  DotMatrix #(.matrixcols(16), .matrixrows(16)) dotmatrix_43 ();  // open: col0, col1, col2, col3, col4, col5, col6, col7, col8, col9, col10, col11, col12, col13, col14, col15
  DotMatrix #(.matrixcols(16), .matrixrows(15)) dotmatrix_44 ();  // open: col0, col1, col2, col3, col4, col5, col6, col7, col8, col9, col10, col11, col12, col13, col14, col15
  DotMatrix #(.matrixcols(16), .matrixrows(16)) dotmatrix_45 ();  // open: col0, col1, col2, col3, col4, col5, col6, col7, col8, col9, col10, col11, col12, col13, col14, col15
  DotMatrix #(.matrixcols(16), .matrixrows(15)) dotmatrix_46 ();  // open: col0, col1, col2, col3, col4, col5, col6, col7, col8, col9, col10, col11, col12, col13, col14, col15
  DotMatrix #(.matrixcols(16), .matrixrows(16)) dotmatrix_47 ();  // open: col0, col1, col2, col3, col4, col5, col6, col7, col8, col9, col10, col11, col12, col13, col14, col15
  DotMatrix #(.matrixcols(16), .matrixrows(15)) dotmatrix_48 ();  // open: col0, col1, col2, col3, col4, col5, col6, col7, col8, col9, col10, col11, col12, col13, col14, col15
  DotMatrix #(.matrixcols(16), .matrixrows(16)) dotmatrix_49 ();  // open: col0, col1, col2, col3, col4, col5, col6, col7, col8, col9, col10, col11, col12, col13, col14, col15
  DotMatrix #(.matrixcols(16), .matrixrows(15)) dotmatrix_50 ();  // open: col0, col1, col2, col3, col4, col5, col6, col7, col8, col9, col10, col11, col12, col13, col14, col15
  DotMatrix #(.matrixcols(16), .matrixrows(16)) dotmatrix_51 ();  // open: col0, col1, col2, col3, col4, col5, col6, col7, col8, col9, col10, col11, col12, col13, col14, col15
  DotMatrix #(.matrixcols(16), .matrixrows(15)) dotmatrix_52 ();  // open: col0, col1, col2, col3, col4, col5, col6, col7, col8, col9, col10, col11, col12, col13, col14, col15
  DotMatrix #(.matrixcols(16), .matrixrows(16)) dotmatrix_53 ();  // open: col0, col1, col2, col3, col4, col5, col6, col7, col8, col9, col10, col11, col12, col13, col14, col15
  Counter #(.width(4), .max('hb), .trigger("falling")) counter_1 (
    .count(enable), .Q(curr_coulumn), .carry(counter_1_carry), .clk(clk), .clr(\end ));  // open: load, D
  Counter #(.width(2), .max('h2), .trigger("falling")) counter_2 (
    .count(enable), .Q({counter_2_q[1], current_cell}), .carry(\end ), .clk(counter_1_carry), .clr(\end ));  // open: load, D
  DotMatrix #(.matrixcols(16), .matrixrows(15)) dotmatrix_54 ();  // open: col0, col1, col2, col3, col4, col5, col6, col7, col8, col9, col10, col11, col12, col13, col14, col15
  DotMatrix #(.matrixcols(16), .matrixrows(16)) dotmatrix_55 ();  // open: col0, col1, col2, col3, col4, col5, col6, col7, col8, col9, col10, col11, col12, col13, col14, col15
  DotMatrix #(.matrixcols(16), .matrixrows(15)) dotmatrix_56 ();  // open: col0, col1, col2, col3, col4, col5, col6, col7, col8, col9, col10, col11, col12, col13, col14, col15
  DotMatrix #(.matrixcols(16), .matrixrows(16)) dotmatrix_57 ();  // open: col0, col1, col2, col3, col4, col5, col6, col7, col8, col9, col10, col11, col12, col13, col14, col15
  DotMatrix #(.matrixcols(16), .matrixrows(15)) dotmatrix_58 ();  // open: col0, col1, col2, col3, col4, col5, col6, col7, col8, col9, col10, col11, col12, col13, col14, col15
  DotMatrix #(.matrixcols(16), .matrixrows(16)) dotmatrix_59 ();  // open: col0, col1, col2, col3, col4, col5, col6, col7, col8, col9, col10, col11, col12, col13, col14, col15
  DotMatrix #(.matrixcols(16), .matrixrows(15)) dotmatrix_60 ();  // open: col0, col1, col2, col3, col4, col5, col6, col7, col8, col9, col10, col11, col12, col13, col14, col15
  DotMatrix #(.matrixcols(16), .matrixrows(16)) dotmatrix_61 ();  // open: col0, col1, col2, col3, col4, col5, col6, col7, col8, col9, col10, col11, col12, col13, col14, col15
  DotMatrix #(.matrixcols(16), .matrixrows(15)) dotmatrix_62 ();  // open: col0, col1, col2, col3, col4, col5, col6, col7, col8, col9, col10, col11, col12, col13, col14, col15
  DotMatrix #(.matrixcols(16), .matrixrows(16)) dotmatrix_63 ();  // open: col0, col1, col2, col3, col4, col5, col6, col7, col8, col9, col10, col11, col12, col13, col14, col15
  DotMatrix #(.matrixcols(16), .matrixrows(15)) dotmatrix_64 ();  // open: col0, col1, col2, col3, col4, col5, col6, col7, col8, col9, col10, col11, col12, col13, col14, col15
  DotMatrix #(.matrixcols(16), .matrixrows(16)) dotmatrix_65 ();  // open: col0, col1, col2, col3, col4, col5, col6, col7, col8, col9, col10, col11, col12, col13, col14, col15
  DotMatrix #(.matrixcols(16), .matrixrows(15)) dotmatrix_66 ();  // open: col0, col1, col2, col3, col4, col5, col6, col7, col8, col9, col10, col11, col12, col13, col14, col15
  DotMatrix #(.matrixcols(16), .matrixrows(16)) dotmatrix_67 ();  // open: col0, col1, col2, col3, col4, col5, col6, col7, col8, col9, col10, col11, col12, col13, col14, col15
  DotMatrix #(.matrixcols(16), .matrixrows(15)) dotmatrix_68 ();  // open: col0, col1, col2, col3, col4, col5, col6, col7, col8, col9, col10, col11, col12, col13, col14, col15
  DotMatrix #(.matrixcols(16), .matrixrows(16)) dotmatrix_69 ();  // open: col0, col1, col2, col3, col4, col5, col6, col7, col8, col9, col10, col11, col12, col13, col14, col15
  D_Flip_Flop d_ff_2 (.clk(inspect), .D(1'b1), .Q(enable), .reset(\end ));  // open: Qn, preset, en
  DotMatrix #(.matrixcols(16), .matrixrows(15)) dotmatrix_70 ();  // open: col0, col1, col2, col3, col4, col5, col6, col7, col8, col9, col10, col11, col12, col13, col14, col15
  DotMatrix #(.matrixcols(16), .matrixrows(16)) dotmatrix_71 ();  // open: col0, col1, col2, col3, col4, col5, col6, col7, col8, col9, col10, col11, col12, col13, col14, col15
  DotMatrix #(.matrixcols(16), .matrixrows(15)) dotmatrix_72 ();  // open: col0, col1, col2, col3, col4, col5, col6, col7, col8, col9, col10, col11, col12, col13, col14, col15
  DotMatrix #(.matrixcols(16), .matrixrows(16)) dotmatrix_73 ();  // open: col0, col1, col2, col3, col4, col5, col6, col7, col8, col9, col10, col11, col12, col13, col14, col15
  DotMatrix #(.matrixcols(16), .matrixrows(15)) dotmatrix_74 ();  // open: col0, col1, col2, col3, col4, col5, col6, col7, col8, col9, col10, col11, col12, col13, col14, col15
  DotMatrix #(.matrixcols(16), .matrixrows(16)) dotmatrix_75 ();  // open: col0, col1, col2, col3, col4, col5, col6, col7, col8, col9, col10, col11, col12, col13, col14, col15
  DotMatrix #(.matrixcols(16), .matrixrows(15)) dotmatrix_76 ();  // open: col0, col1, col2, col3, col4, col5, col6, col7, col8, col9, col10, col11, col12, col13, col14, col15
  DotMatrix #(.matrixcols(16), .matrixrows(16)) dotmatrix_77 ();  // open: col0, col1, col2, col3, col4, col5, col6, col7, col8, col9, col10, col11, col12, col13, col14, col15
  DotMatrix #(.matrixcols(16), .matrixrows(15)) dotmatrix_78 ();  // open: col0, col1, col2, col3, col4, col5, col6, col7, col8, col9, col10, col11, col12, col13, col14, col15
  DotMatrix #(.matrixcols(16), .matrixrows(16)) dotmatrix_79 ();  // open: col0, col1, col2, col3, col4, col5, col6, col7, col8, col9, col10, col11, col12, col13, col14, col15
  DotMatrix #(.matrixcols(16), .matrixrows(15)) dotmatrix_80 ();  // open: col0, col1, col2, col3, col4, col5, col6, col7, col8, col9, col10, col11, col12, col13, col14, col15
  DotMatrix #(.matrixcols(16), .matrixrows(16)) dotmatrix_81 ();  // open: col0, col1, col2, col3, col4, col5, col6, col7, col8, col9, col10, col11, col12, col13, col14, col15
  DotMatrix #(.matrixcols(16), .matrixrows(15)) dotmatrix_82 ();  // open: col0, col1, col2, col3, col4, col5, col6, col7, col8, col9, col10, col11, col12, col13, col14, col15
  DotMatrix #(.matrixcols(16), .matrixrows(16)) dotmatrix_83 ();  // open: col0, col1, col2, col3, col4, col5, col6, col7, col8, col9, col10, col11, col12, col13, col14, col15
  DotMatrix #(.matrixcols(16), .matrixrows(15)) dotmatrix_84 ();  // open: col0, col1, col2, col3, col4, col5, col6, col7, col8, col9, col10, col11, col12, col13, col14, col15
  DotMatrix #(.matrixcols(16), .matrixrows(16)) dotmatrix_85 ();  // open: col0, col1, col2, col3, col4, col5, col6, col7, col8, col9, col10, col11, col12, col13, col14, col15
  DotMatrix #(.matrixcols(16), .matrixrows(15)) dotmatrix_86 ();  // open: col0, col1, col2, col3, col4, col5, col6, col7, col8, col9, col10, col11, col12, col13, col14, col15
  DotMatrix #(.matrixcols(16), .matrixrows(16)) dotmatrix_87 ();  // open: col0, col1, col2, col3, col4, col5, col6, col7, col8, col9, col10, col11, col12, col13, col14, col15
  DotMatrix #(.matrixcols(16), .matrixrows(15)) dotmatrix_88 ();  // open: col0, col1, col2, col3, col4, col5, col6, col7, col8, col9, col10, col11, col12, col13, col14, col15
  DotMatrix #(.matrixcols(16), .matrixrows(16)) dotmatrix_89 ();  // open: col0, col1, col2, col3, col4, col5, col6, col7, col8, col9, col10, col11, col12, col13, col14, col15
  DotMatrix #(.matrixcols(16), .matrixrows(15)) dotmatrix_90 ();  // open: col0, col1, col2, col3, col4, col5, col6, col7, col8, col9, col10, col11, col12, col13, col14, col15
  DotMatrix #(.matrixcols(16), .matrixrows(16)) dotmatrix_91 ();  // open: col0, col1, col2, col3, col4, col5, col6, col7, col8, col9, col10, col11, col12, col13, col14, col15
  DotMatrix #(.matrixcols(16), .matrixrows(15)) dotmatrix_92 ();  // open: col0, col1, col2, col3, col4, col5, col6, col7, col8, col9, col10, col11, col12, col13, col14, col15
  DotMatrix #(.matrixcols(16), .matrixrows(16)) dotmatrix_93 ();  // open: col0, col1, col2, col3, col4, col5, col6, col7, col8, col9, col10, col11, col12, col13, col14, col15
  DotMatrix #(.matrixcols(16), .matrixrows(15)) dotmatrix_94 ();  // open: col0, col1, col2, col3, col4, col5, col6, col7, col8, col9, col10, col11, col12, col13, col14, col15
  DotMatrix #(.matrixcols(16), .matrixrows(16)) dotmatrix_95 ();  // open: col0, col1, col2, col3, col4, col5, col6, col7, col8, col9, col10, col11, col12, col13, col14, col15
  DotMatrix #(.matrixcols(16), .matrixrows(15)) dotmatrix_96 ();  // open: col0, col1, col2, col3, col4, col5, col6, col7, col8, col9, col10, col11, col12, col13, col14, col15
  DotMatrix #(.matrixcols(16), .matrixrows(16)) dotmatrix_97 ();  // open: col0, col1, col2, col3, col4, col5, col6, col7, col8, col9, col10, col11, col12, col13, col14, col15
  DotMatrix #(.matrixcols(16), .matrixrows(15)) dotmatrix_98 ();  // open: col0, col1, col2, col3, col4, col5, col6, col7, col8, col9, col10, col11, col12, col13, col14, col15
  DotMatrix #(.matrixcols(16), .matrixrows(16)) dotmatrix_99 ();  // open: col0, col1, col2, col3, col4, col5, col6, col7, col8, col9, col10, col11, col12, col13, col14, col15
  DotMatrix #(.matrixcols(16), .matrixrows(15)) dotmatrix_100 ();  // open: col0, col1, col2, col3, col4, col5, col6, col7, col8, col9, col10, col11, col12, col13, col14, col15
  DotMatrix #(.matrixcols(16), .matrixrows(16)) dotmatrix_101 ();  // open: col0, col1, col2, col3, col4, col5, col6, col7, col8, col9, col10, col11, col12, col13, col14, col15
  DotMatrix #(.matrixcols(16), .matrixrows(15)) dotmatrix_102 ();  // open: col0, col1, col2, col3, col4, col5, col6, col7, col8, col9, col10, col11, col12, col13, col14, col15
  DotMatrix #(.matrixcols(16), .matrixrows(16)) dotmatrix_103 ();  // open: col0, col1, col2, col3, col4, col5, col6, col7, col8, col9, col10, col11, col12, col13, col14, col15
  DotMatrix #(.matrixcols(16), .matrixrows(15)) dotmatrix_104 ();  // open: col0, col1, col2, col3, col4, col5, col6, col7, col8, col9, col10, col11, col12, col13, col14, col15
  DotMatrix #(.matrixcols(16), .matrixrows(16)) dotmatrix_105 ();  // open: col0, col1, col2, col3, col4, col5, col6, col7, col8, col9, col10, col11, col12, col13, col14, col15
  DotMatrix #(.matrixcols(16), .matrixrows(15)) dotmatrix_106 ();  // open: col0, col1, col2, col3, col4, col5, col6, col7, col8, col9, col10, col11, col12, col13, col14, col15
  DotMatrix #(.matrixcols(16), .matrixrows(16)) dotmatrix_107 ();  // open: col0, col1, col2, col3, col4, col5, col6, col7, col8, col9, col10, col11, col12, col13, col14, col15
  DotMatrix #(.matrixcols(16), .matrixrows(15)) dotmatrix_108 ();  // open: col0, col1, col2, col3, col4, col5, col6, col7, col8, col9, col10, col11, col12, col13, col14, col15
  DotMatrix #(.matrixcols(16), .matrixrows(16)) dotmatrix_109 ();  // open: col0, col1, col2, col3, col4, col5, col6, col7, col8, col9, col10, col11, col12, col13, col14, col15
  DotMatrix #(.matrixcols(16), .matrixrows(15)) dotmatrix_110 ();  // open: col0, col1, col2, col3, col4, col5, col6, col7, col8, col9, col10, col11, col12, col13, col14, col15
  DotMatrix #(.matrixcols(16), .matrixrows(16)) dotmatrix_111 ();  // open: col0, col1, col2, col3, col4, col5, col6, col7, col8, col9, col10, col11, col12, col13, col14, col15
  DotMatrix #(.matrixcols(16), .matrixrows(15)) dotmatrix_112 ();  // open: col0, col1, col2, col3, col4, col5, col6, col7, col8, col9, col10, col11, col12, col13, col14, col15
  DotMatrix #(.matrixcols(16), .matrixrows(16)) dotmatrix_113 ();  // open: col0, col1, col2, col3, col4, col5, col6, col7, col8, col9, col10, col11, col12, col13, col14, col15
  DotMatrix #(.matrixcols(16), .matrixrows(15)) dotmatrix_114 ();  // open: col0, col1, col2, col3, col4, col5, col6, col7, col8, col9, col10, col11, col12, col13, col14, col15
  DotMatrix #(.matrixcols(16), .matrixrows(16)) dotmatrix_115 ();  // open: col0, col1, col2, col3, col4, col5, col6, col7, col8, col9, col10, col11, col12, col13, col14, col15
  DotMatrix #(.matrixcols(16), .matrixrows(15)) dotmatrix_116 ();  // open: col0, col1, col2, col3, col4, col5, col6, col7, col8, col9, col10, col11, col12, col13, col14, col15
  DotMatrix #(.matrixcols(16), .matrixrows(16)) dotmatrix_117 ();  // open: col0, col1, col2, col3, col4, col5, col6, col7, col8, col9, col10, col11, col12, col13, col14, col15
  DotMatrix #(.matrixcols(16), .matrixrows(15)) dotmatrix_118 ();  // open: col0, col1, col2, col3, col4, col5, col6, col7, col8, col9, col10, col11, col12, col13, col14, col15
  DotMatrix #(.matrixcols(16), .matrixrows(16)) dotmatrix_119 ();  // open: col0, col1, col2, col3, col4, col5, col6, col7, col8, col9, col10, col11, col12, col13, col14, col15
  DotMatrix #(.matrixcols(16), .matrixrows(15)) dotmatrix_120 ();  // open: col0, col1, col2, col3, col4, col5, col6, col7, col8, col9, col10, col11, col12, col13, col14, col15
  DotMatrix #(.matrixcols(16), .matrixrows(16)) dotmatrix_121 ();  // open: col0, col1, col2, col3, col4, col5, col6, col7, col8, col9, col10, col11, col12, col13, col14, col15
  DotMatrix #(.matrixcols(16), .matrixrows(15)) dotmatrix_122 ();  // open: col0, col1, col2, col3, col4, col5, col6, col7, col8, col9, col10, col11, col12, col13, col14, col15
  DotMatrix #(.matrixcols(16), .matrixrows(16)) dotmatrix_123 ();  // open: col0, col1, col2, col3, col4, col5, col6, col7, col8, col9, col10, col11, col12, col13, col14, col15
  DotMatrix #(.matrixcols(16), .matrixrows(15)) dotmatrix_124 ();  // open: col0, col1, col2, col3, col4, col5, col6, col7, col8, col9, col10, col11, col12, col13, col14, col15
  DotMatrix #(.matrixcols(16), .matrixrows(16)) dotmatrix_125 ();  // open: col0, col1, col2, col3, col4, col5, col6, col7, col8, col9, col10, col11, col12, col13, col14, col15
  DotMatrix #(.matrixcols(16), .matrixrows(15)) dotmatrix_126 ();  // open: col0, col1, col2, col3, col4, col5, col6, col7, col8, col9, col10, col11, col12, col13, col14, col15
  DotMatrix #(.matrixcols(16), .matrixrows(16)) dotmatrix_127 ();  // open: col0, col1, col2, col3, col4, col5, col6, col7, col8, col9, col10, col11, col12, col13, col14, col15
  DotMatrix #(.matrixcols(16), .matrixrows(15)) dotmatrix_128 ();  // open: col0, col1, col2, col3, col4, col5, col6, col7, col8, col9, col10, col11, col12, col13, col14, col15
  DotMatrix #(.matrixcols(16), .matrixrows(16)) dotmatrix_129 ();  // open: col0, col1, col2, col3, col4, col5, col6, col7, col8, col9, col10, col11, col12, col13, col14, col15
  DotMatrix #(.matrixcols(16), .matrixrows(15)) dotmatrix_130 ();  // open: col0, col1, col2, col3, col4, col5, col6, col7, col8, col9, col10, col11, col12, col13, col14, col15
  DotMatrix #(.matrixcols(16), .matrixrows(16)) dotmatrix_131 ();  // open: col0, col1, col2, col3, col4, col5, col6, col7, col8, col9, col10, col11, col12, col13, col14, col15
  DotMatrix #(.matrixcols(16), .matrixrows(15)) dotmatrix_132 ();  // open: col0, col1, col2, col3, col4, col5, col6, col7, col8, col9, col10, col11, col12, col13, col14, col15
  DotMatrix #(.matrixcols(16), .matrixrows(16)) dotmatrix_133 ();  // open: col0, col1, col2, col3, col4, col5, col6, col7, col8, col9, col10, col11, col12, col13, col14, col15

  // Other names for the same wires on the sheet: input_signal = enter

  // Notes on the sheet:
  //   TODO
  //   set queen if figure not write
  //   0 nothing
  //   1 check
  //   2 checkmate
  //   3 stalemate
  //   4 invalid
  //   0 nothing
  //   1 check
  //   2 checkmate
  //   3 stalemate
  //   4 invalid
endmodule

module IdentMove (
  input  [6:0] symbol,
  input  symbol_update,
  input  reset,
  output [15:0] out_4
);

  wire comparator_1_eq, comparator_2_eq, comparator_3_eq, comparator_4_eq, decoder_1_out0, decoder_1_out1,
       decoder_1_out2, decoder_1_out3, decoder_1_out4;
  wire [1:0] priority_encoder_1_out;
  wire [2:0] bit_extender_1_out, counter_1_q, multiplexer_2_out, not_1_out;
  wire [3:0] multiplexer_3_out;
  wire [6:0] multiplexer_1_out, subtractor_1_out;

  Counter #(.width(3), .max('h5), .trigger("falling")) counter_1 (
    .Q(counter_1_q), .clk(symbol_update), .clr(reset));  // open: load, D, count, carry
  Multiplexer #(.width(7), .enable("false")) multiplexer_1 (
    .in0(7'b1000001), .in1(7'b0110001), .out(multiplexer_1_out), .sel(counter_1_q[0]));
  Decoder #(.select(3)) decoder_1 (
    .out0(decoder_1_out0), .out1(decoder_1_out1), .out2(decoder_1_out2), .out3(decoder_1_out3),
    .out4(decoder_1_out4), .sel(counter_1_q));  // open: out5, out6, out7, en
  Subtractor #(.width(7)) subtractor_1 (
    .a(symbol), .b(multiplexer_1_out), .out(subtractor_1_out), .bin(1'b0));  // open: bout
  Comparator #(.width(7)) comparator_1 (.a(7'b1010001), .b(symbol), .eq(comparator_1_eq));  // open: gt, lt
  Comparator #(.width(7)) comparator_2 (.a(7'b1010010), .b(symbol), .eq(comparator_2_eq));  // open: gt, lt
  Comparator #(.width(7)) comparator_3 (.a(7'b1000010), .b(symbol), .eq(comparator_3_eq));  // open: gt, lt
  Comparator #(.width(7)) comparator_4 (.a(7'b1001110), .b(symbol), .eq(comparator_4_eq));  // open: gt, lt
  Bit_Extender #(.in_width(7), .out_width(3)) bit_extender_1 (.in(subtractor_1_out), .out(bit_extender_1_out));
  Multiplexer #(.width(3), .enable("false")) multiplexer_2 (
    .in0(bit_extender_1_out), .in1(not_1_out), .out(multiplexer_2_out), .sel(counter_1_q[0]));
  assign not_1_out = ~bit_extender_1_out;  // NOT_Gate not_1, 3 bits wide
  Priority_Encoder #(.select(2)) priority_encoder_1 (
    .in0(comparator_1_eq), .in1(comparator_2_eq), .in2(comparator_3_eq), .in3(comparator_4_eq),
    .out(priority_encoder_1_out));  // open: gs, en_out, en_in
  Multiplexer #(.select(2), .width(4)) multiplexer_3 (
    .in0(4'b1011), .in1(4'b1101), .in2(4'b0110), .in3(4'b1110), .out(multiplexer_3_out),
    .sel(priority_encoder_1_out));  // open: en
  Register #(.width(3), .trigger("falling")) register_1 (
    .D(multiplexer_2_out), .en(decoder_1_out0), .Q(out_4[2:0]), .clk(symbol_update), .clr(reset));
  Register #(.width(3), .trigger("falling")) register_2 (
    .D(multiplexer_2_out), .en(decoder_1_out1), .Q(out_4[5:3]), .clk(symbol_update), .clr(reset));
  Register #(.width(3), .trigger("falling")) register_3 (
    .D(multiplexer_2_out), .en(decoder_1_out2), .Q(out_4[8:6]), .clk(symbol_update), .clr(reset));
  Register #(.width(3), .trigger("falling")) register_4 (
    .D(multiplexer_2_out), .en(decoder_1_out3), .Q(out_4[11:9]), .clk(symbol_update), .clr(reset));
  Register #(.width(4), .trigger("falling")) register_5 (
    .D(multiplexer_3_out), .en(decoder_1_out4), .Q(out_4[15:12]), .clk(symbol_update));  // open: clr
endmodule

module button_pad (
  input  in_1,
  input  in_2,
  input  in_3,
  input  in_4,
  input  in_5,
  input  in_6,
  input  in_7,
  input  in_8,
  input  in_9,
  input  in_10,
  input  in_11,
  input  in_12,
  input  in_13,
  input  in_14,
  input  in_15,
  input  in_16,
  input  in_17,
  input  in_18,
  input  in_19,
  input  in_20,
  input  in_21,
  input  in_22,
  input  in_23,
  input  in_24,
  input  in_25,
  input  in_26,
  input  in_27,
  input  in_28,
  input  in_29,
  input  in_30,
  input  in_31,
  input  in_32,
  input  in_33,
  input  in_34,
  input  in_35,
  input  in_36,
  input  in_37,
  input  in_38,
  input  in_39,
  input  in_40,
  input  in_41,
  input  in_42,
  input  in_43,
  input  in_44,
  input  in_45,
  input  in_46,
  input  in_47,
  input  in_48,
  input  in_49,
  input  in_50,
  input  in_51,
  input  in_52,
  input  in_53,
  input  in_54,
  input  in_55,
  input  in_56,
  input  in_57,
  input  in_58,
  input  in_59,
  input  in_60,
  input  in_61,
  input  in_62,
  input  in_63,
  input  in_64,
  output [2:0] X,
  output [2:0] Y,
  output pressed
);

  wire bitfinder_1_found, bitfinder_2_found, bitfinder_3_found, bitfinder_4_found, bitfinder_5_found,
       bitfinder_6_found, bitfinder_7_found, bitfinder_8_found, buffer_1_out, buffer_2_out, buffer_3_out,
       buffer_4_out, priority_encoder_1_gs;
  wire [2:0] bitfinder_1_index, bitfinder_2_index, bitfinder_3_index, bitfinder_4_index, bitfinder_5_index,
       bitfinder_6_index, bitfinder_7_index, bitfinder_8_index;

  BitFinder bitfinder_1 (
    .in({in_8, in_7, in_6, in_5, in_4, in_3, in_2, in_1}), .index(bitfinder_1_index),
    .found(bitfinder_1_found));
  BitFinder bitfinder_2 (
    .in({in_16, in_15, in_14, in_13, in_12, in_11, in_10, in_9}), .index(bitfinder_2_index),
    .found(bitfinder_2_found));
  BitFinder bitfinder_3 (
    .in({in_24, in_23, in_22, in_21, in_20, in_19, in_18, in_17}), .index(bitfinder_3_index),
    .found(bitfinder_3_found));
  BitFinder bitfinder_4 (
    .in({in_32, in_31, in_30, in_29, in_28, in_27, in_26, in_25}), .index(bitfinder_4_index),
    .found(bitfinder_4_found));
  BitFinder bitfinder_5 (
    .in({in_40, in_39, in_38, in_37, in_36, in_35, in_34, in_33}), .index(bitfinder_5_index),
    .found(bitfinder_5_found));
  BitFinder bitfinder_6 (
    .in({in_48, in_47, in_46, in_45, in_44, in_43, in_42, in_41}), .index(bitfinder_6_index),
    .found(bitfinder_6_found));
  BitFinder bitfinder_7 (
    .in({in_56, in_55, in_54, in_53, in_52, in_51, in_50, in_49}), .index(bitfinder_7_index),
    .found(bitfinder_7_found));
  BitFinder bitfinder_8 (
    .in({in_64, in_63, in_62, in_61, in_60, in_59, in_58, in_57}), .index(bitfinder_8_index),
    .found(bitfinder_8_found));
  Multiplexer #(.select(3), .width(3), .disabled(0), .enable("false")) multiplexer_1 (
    .in0(bitfinder_1_index), .in1(bitfinder_2_index), .in2(bitfinder_3_index), .in3(bitfinder_4_index),
    .in4(bitfinder_5_index), .in5(bitfinder_6_index), .in6(bitfinder_7_index), .in7(bitfinder_8_index),
    .out(X), .sel(Y));
  Pull_Resistor pull_resistor_1 (.node(Y));
  Priority_Encoder #(.disabled(0)) priority_encoder_1 (
    .in0(bitfinder_1_found), .in1(bitfinder_2_found), .in2(bitfinder_3_found), .in3(bitfinder_4_found),
    .in4(bitfinder_5_found), .in5(bitfinder_6_found), .in6(bitfinder_7_found), .in7(bitfinder_8_found),
    .out(Y), .gs(priority_encoder_1_gs));  // open: en_in, en_out
  buf buffer_1 (buffer_1_out, priority_encoder_1_gs);
  buf buffer_2 (buffer_2_out, buffer_1_out);
  buf buffer_3 (buffer_3_out, buffer_2_out);
  buf buffer_4 (buffer_4_out, buffer_3_out);
  buf buffer_5 (pressed, buffer_4_out);
endmodule

module button_ident (
  input  [3:0] figure,
  input  [5:0] button,
  input  update,
  input  figure_update,
  input  reset,
  output [15:0] step_info
);

  wire counter_1_q, decoder_1_out0, decoder_1_out1;

  Counter #(.width(1), .max('h1)) counter_1 (
    .Q(counter_1_q), .clk(update), .clr(reset));  // open: load, D, count, carry
  Decoder #(.disabled(0), .enable("false")) decoder_1 (.out0(decoder_1_out0), .out1(decoder_1_out1), .sel(counter_1_q));
  Register #(.width(6)) register_1 (.D(button), .en(decoder_1_out0), .Q(step_info[5:0]), .clk(update), .clr(reset));
  Register #(.width(6)) register_2 (.D(button), .en(decoder_1_out1), .Q(step_info[11:6]), .clk(update), .clr(reset));
  Register #(.width(4), .trigger("falling")) register_3 (
    .D(figure), .Q(step_info[15:12]), .clk(figure_update), .clr(reset));  // open: en
endmodule

module figure_pad (
  input  Knight,
  input  Bishop,
  input  Rock,
  input  Queen,
  output [3:0] figure,
  output figure_signal
);

  assign figure = Knight ? 4'b1110 : 4'bz;  // Controlled_Buffer controlled_buffer_1
  assign figure = Bishop ? 4'b0110 : 4'bz;  // Controlled_Buffer controlled_buffer_2
  assign figure = Rock ? 4'b1101 : 4'bz;  // Controlled_Buffer controlled_buffer_3
  assign figure = Queen ? 4'b1011 : 4'bz;  // Controlled_Buffer controlled_buffer_4
  BitFinder #(.width(4)) bitfinder_1 (.in(figure), .found(figure_signal));  // open: index
  Pull_Resistor pull_resistor_1 (.node(figure));
endmodule

module LastMove (
  input  [15:0] in_1,
  output [6:0] _1,
  output [6:0] out_3,
  output [6:0] out_4,
  output [6:0] out_5,
  output [6:0] out_6,
  output [6:0] _2,
  output [6:0] out_8,
  output [6:0] out_9,
  output [6:0] out_10,
  output [6:0] out_11,
  output [6:0] _3,
  output [6:0] out_13,
  output [6:0] out_14,
  output [6:0] out_15,
  output [6:0] out_16,
  output [6:0] _4,
  output [6:0] out_18,
  output [6:0] out_19,
  output [6:0] out_20,
  output [6:0] out_21,
  output [6:0] _5,
  output [6:0] out_23,
  output [6:0] out_24,
  output [6:0] out_25,
  output [6:0] out_26,
  output [6:0] _6,
  output [6:0] out_28,
  output [6:0] out_29,
  output [6:0] out_30,
  output [6:0] out_31
);

  DotMatrix #(.matrixcols(6), .matrixrows(5)) dotmatrix_1 (
    .col0({5{1'b0}}), .col1(5'b01111), .col2(5'b10010), .col3(5'b10010), .col4(5'b01111), .col5({5{1'b0}}));
  DotMatrix #(.matrixcols(6), .matrixrows(5)) dotmatrix_2 (
    .col0({5{1'b0}}), .col1({5{1'b1}}), .col2(5'b10101), .col3(5'b11101), .col4(5'b00111), .col5({5{1'b0}}));
  DotMatrix #(.matrixcols(6), .matrixrows(5)) dotmatrix_3 (
    .col0({5{1'b0}}), .col1(5'b01110), .col2(5'b10001), .col3(5'b10001), .col4(5'b01010), .col5({5{1'b0}}));
  DotMatrix #(.matrixcols(6), .matrixrows(5)) dotmatrix_4 (
    .col0({5{1'b0}}), .col1({5{1'b1}}), .col2(5'b10001), .col3(5'b10001), .col4(5'b01110), .col5({5{1'b0}}));
  DotMatrix #(.matrixcols(6), .matrixrows(5)) dotmatrix_5 (
    .col0({5{1'b0}}), .col1({5{1'b1}}), .col2(5'b10101), .col3(5'b10101), .col4(5'b10101), .col5({5{1'b0}}));
  DotMatrix #(.matrixcols(6), .matrixrows(5)) dotmatrix_6 (
    .col0({5{1'b0}}), .col1({5{1'b1}}), .col2(5'b10100), .col3(5'b10100), .col4(5'b10000), .col5({5{1'b0}}));
  DotMatrix #(.matrixcols(6), .matrixrows(5)) dotmatrix_7 (
    .col0({5{1'b0}}), .col1(5'b01110), .col2(5'b10001), .col3(5'b10101), .col4(5'b10111), .col5({5{1'b0}}));
  DotMatrix #(.matrixcols(6), .matrixrows(5)) dotmatrix_8 (
    .col0({5{1'b0}}), .col1({5{1'b1}}), .col2(5'b00100), .col3(5'b00100), .col4({5{1'b1}}), .col5({5{1'b0}}));
  Multiplexer #(.select(3), .width(30)) multiplexer_1 (
    .in0(30'hf949e0), .in1(30'h7ed7e0), .in2(30'ha8c5c0), .in3(30'he8c7e0), .in4(30'h15ad7e0),
    .in5(30'h10a53e0), .in6(30'h17ac5c0), .in7(30'h1f213e0),
    .out({_6[5:1], _5[5:1], _4[5:1], _3[5:1], _2[5:1], _1[5:1]}), .sel(in_1[2:0]));  // open: en
  Multiplexer #(.select(3), .width(30)) multiplexer_2 (
    .in0(30'hf949e0), .in1(30'h7ed7e0), .in2(30'ha8c5c0), .in3(30'he8c7e0), .in4(30'h15ad7e0),
    .in5(30'h10a53e0), .in6(30'h17ac5c0), .in7(30'h1f213e0),
    .out({out_28[5:1], out_23[5:1], out_18[5:1], out_13[5:1], out_8[5:1], out_3[5:1]}), .sel(in_1[8:6]));  // open: en
  DotMatrix #(.matrixcols(6), .matrixrows(5)) dotmatrix_9 (
    .col0({5{1'b0}}), .col1({5{1'b0}}), .col2(5'b01001), .col3({5{1'b1}}), .col4(5'b00001), .col5({5{1'b0}}));
  DotMatrix #(.matrixcols(6), .matrixrows(5)) dotmatrix_10 (
    .col0({5{1'b0}}), .col1(5'b01001), .col2(5'b10011), .col3(5'b10101), .col4(5'b01001), .col5({5{1'b0}}));
  DotMatrix #(.matrixcols(6), .matrixrows(5)) dotmatrix_11 (
    .col0({5{1'b0}}), .col1(5'b10001), .col2(5'b10101), .col3(5'b10101), .col4(5'b01010), .col5({5{1'b0}}));
  DotMatrix #(.matrixcols(6), .matrixrows(5)) dotmatrix_12 (
    .col0({5{1'b0}}), .col1(5'b00110), .col2(5'b01010), .col3(5'b10010), .col4({5{1'b1}}), .col5({5{1'b0}}));
  DotMatrix #(.matrixcols(6), .matrixrows(5)) dotmatrix_13 (
    .col0({5{1'b0}}), .col1(5'b11101), .col2(5'b10101), .col3(5'b10101), .col4(5'b10110), .col5({5{1'b0}}));
  DotMatrix #(.matrixcols(6), .matrixrows(5)) dotmatrix_14 (
    .col0({5{1'b0}}), .col1(5'b01110), .col2(5'b10101), .col3(5'b10101), .col4(5'b00010), .col5({5{1'b0}}));
  DotMatrix #(.matrixcols(6), .matrixrows(5)) dotmatrix_15 (
    .col0({5{1'b0}}), .col1(5'b11000), .col2(5'b10011), .col3(5'b10100), .col4(5'b11000), .col5({5{1'b0}}));
  DotMatrix #(.matrixcols(6), .matrixrows(5)) dotmatrix_16 (
    .col0({5{1'b0}}), .col1(5'b01010), .col2(5'b10101), .col3(5'b10101), .col4(5'b01010), .col5({5{1'b0}}));
  Multiplexer #(.select(3), .width(30)) multiplexer_3 (
    .in0(30'haad540), .in1(30'h18a4f00), .in2(30'h2ad5c0), .in3(30'h16ad7a0), .in4(30'h1f928c0),
    .in5(30'haad620), .in6(30'h9acd20), .in7(30'h1fa400),
    .out({out_29[5:1], out_24[5:1], out_19[5:1], out_14[5:1], out_9[5:1], out_4[5:1]}), .sel(in_1[11:9]));  // open: en
  Multiplexer #(.select(3), .width(30)) multiplexer_4 (
    .in0(30'haad540), .in1(30'h18a4f00), .in2(30'h2ad5c0), .in3(30'h16ad7a0), .in4(30'h1f928c0),
    .in5(30'haad620), .in6(30'h9acd20), .in7(30'h1fa400),
    .out({out_30[5:1], out_25[5:1], out_20[5:1], out_15[5:1], out_10[5:1], out_5[5:1]}), .sel(in_1[5:3]));  // open: en
  DotMatrix #(.matrixcols(6), .matrixrows(5)) dotmatrix_17 (
    .col0({5{1'b0}}), .col1({5{1'b1}}), .col2(5'b10100), .col3(5'b10100), .col4(5'b01011), .col5({5{1'b0}}));
  DotMatrix #(.matrixcols(6), .matrixrows(5)) dotmatrix_18 (
    .col0({5{1'b0}}), .col1({5{1'b1}}), .col2(5'b10101), .col3(5'b11101), .col4(5'b00111), .col5({5{1'b0}}));
  DotMatrix #(.matrixcols(6), .matrixrows(5)) dotmatrix_19 (
    .col0({5{1'b0}}), .col1({5{1'b1}}), .col2(5'b00100), .col3(5'b00100), .col4(5'b11011), .col5({5{1'b0}}));
  DotMatrix #(.matrixcols(6), .matrixrows(5)) dotmatrix_20 (
    .col0({5{1'b0}}), .col1({5{1'b1}}), .col2(5'b10001), .col3(5'b10010), .col4(5'b11101), .col5({5{1'b0}}));
  Multiplexer #(.select(4), .width(30)) multiplexer_5 (
    .in0({30{1'b0}}), .in1({30{1'b0}}), .in2({30{1'b0}}), .in3({30{1'b0}}), .in4({30{1'b0}}),
    .in5({30{1'b0}}), .in6(30'h7ed7e0), .in7({30{1'b0}}), .in8({30{1'b0}}), .in9({30{1'b0}}),
    .in10({30{1'b0}}), .in11(30'h1d947e0), .in12({30{1'b0}}), .in13(30'hba53e0), .in14(30'h1b213e0),
    .in15({30{1'b0}}), .out({out_31[5:1], out_26[5:1], out_21[5:1], out_16[5:1], out_11[5:1], out_6[5:1]}),
    .sel(in_1[15:12]));  // open: en

  assign {_1[6], _1[0]} = 2'b00;
  assign {_2[6], _2[0]} = 2'b00;
  assign {_3[6], _3[0]} = 2'b00;
  assign {_4[6], _4[0]} = 2'b00;
  assign {_5[6], _5[0]} = 2'b00;
  assign {_6[6], _6[0]} = 2'b00;
  assign {out_3[6], out_3[0]} = 2'b00;
  assign {out_4[6], out_4[0]} = 2'b00;
  assign {out_5[6], out_5[0]} = 2'b00;
  assign {out_6[6], out_6[0]} = 2'b00;
  assign {out_8[6], out_8[0]} = 2'b00;
  assign {out_9[6], out_9[0]} = 2'b00;
  assign {out_10[6], out_10[0]} = 2'b00;
  assign {out_11[6], out_11[0]} = 2'b00;
  assign {out_13[6], out_13[0]} = 2'b00;
  assign {out_14[6], out_14[0]} = 2'b00;
  assign {out_15[6], out_15[0]} = 2'b00;
  assign {out_16[6], out_16[0]} = 2'b00;
  assign {out_18[6], out_18[0]} = 2'b00;
  assign {out_19[6], out_19[0]} = 2'b00;
  assign {out_20[6], out_20[0]} = 2'b00;
  assign {out_21[6], out_21[0]} = 2'b00;
  assign {out_23[6], out_23[0]} = 2'b00;
  assign {out_24[6], out_24[0]} = 2'b00;
  assign {out_25[6], out_25[0]} = 2'b00;
  assign {out_26[6], out_26[0]} = 2'b00;
  assign {out_28[6], out_28[0]} = 2'b00;
  assign {out_29[6], out_29[0]} = 2'b00;
  assign {out_30[6], out_30[0]} = 2'b00;
  assign {out_31[6], out_31[0]} = 2'b00;

  // Other names for the same wires on the sheet: _1_t[2:0] = in_1[2:0]; _2_t[2:0] = in_1[5:3]; _3_t[2:0] = in_1[8:6];
  //   _4_t[2:0] = in_1[11:9]; _5_t[3:0] = in_1[15:12]
endmodule
